# Fritzing sketch 回路図 (saved by Fritzing 0.9.9b)
circuit board: 8.46667cm x 5.64444cm
breadboards: 1

parts:
  PIC16F1459 = PICAXE-20M [package=THT]
  JP1 = USB_MICROB_PLUG [package=micro-b-ra-smt]
  C1 = Ceramic Capacitor [capacitance=100nF voltage=35V package="100 mil [THT, multilayer]"]
  SW1 = female pin header, 2 pins [form="♀ (female)"]
  SW2 = female pin header, 2 pins [form="♀ (female)"]
  SW3 = female pin header, 2 pins [form="♀ (female)"]
  SW4 = female pin header, 2 pins [form="♀ (female)"]
  J5 = female pin header, 2 pins [form="♀ (female)"]
  R5 = Resistor [tolerance=±5% power=0.25 resistance=220 package=THT]
  J6 = female pin header, 2 pins [form="♀ (female)"]
  R6 = Resistor [tolerance=±5% power=0.25 resistance=220 package=THT]
  J7 = female pin header, 2 pins [form="♀ (female)"]
  J8 = female pin header, 2 pins [form="♀ (female)"]
  R7 = Resistor [tolerance=±5% power=0.25 resistance=220 package=THT]
  R8 = Resistor [tolerance=±5% power=0.25 resistance=220 package=THT]
  R9 = Resistor [tolerance=±5% power=0.25 resistance=220 package=THT]
  R10 = Resistor [tolerance=±5% power=0.25 resistance=220 package=THT]
  J9 = female pin header, 2 pins [form="♀ (female)"]
  J10 = female pin header, 2 pins [form="♀ (female)"]
  J11 = female pin header, 2 pins [form="♀ (female)"]
  J12 = female pin header, 2 pins [form="♀ (female)"]
  R11 = Resistor [tolerance=±5% power=0.25 resistance=220 package=THT]
  R12 = Resistor [tolerance=±5% power=0.25 resistance=220 package=THT]

nets:
  N1: PIC16F1459.+V, JP1.VCC, C1.0
  N2: PIC16F1459.Serial_In, SW1.pin1
  N3: PIC16F1459.In_7_/_ADC_7, SW2.pin1
  N4: PIC16F1459.In_6, SW3.pin1
  N5: PIC16F1459.In_5, R6.Pin_1
  N6: PIC16F1459.In_4, R5.Pin_1
  N7: PIC16F1459.In_3_/_ADC_3, R12.Pin_0
  N8: PIC16F1459.In_2_/_ADC_2, R7.Pin_1
  N9: PIC16F1459.In_1_/_ADC_1, R8.Pin_1
  N10: PIC16F1459.In_0_/_Infrain, SW4.pin1
  N11: PIC16F1459.Out_4, R11.Pin_0
  N12: PIC16F1459.Out_3, R10.Pin_0
  N13: PIC16F1459.Out_2, R9.Pin_0
  N14: PIC16F1459.Out_0_/_Infraout, JP1.D-
  N15: PIC16F1459.Serial_Out, JP1.D+
  N16: PIC16F1459.0V, JP1.GND, C1.1, SW1.pin2, SW2.pin2, SW3.pin2, SW4.pin2, J5.pin2, J6.pin2, J7.pin2, J8.pin2, J9.pin2, J10.pin2, J11.pin1, J12.pin1
  N17: J5.pin1, R5.Pin_0
  N18: J6.pin1, R6.Pin_0
  N19: J7.pin1, R7.Pin_0
  N20: J8.pin1, R8.Pin_0
  N21: R9.Pin_1, J10.pin1
  N22: R10.Pin_1, J9.pin1
  N23: J11.pin2, R11.Pin_1
  N24: J12.pin2, R12.Pin_1
